# Fritzing sketch fritzing dosyası (saved by Fritzing 0.9.9b)

parts:
  Parça1 = Arduino Nano (Rev3.0)
  Keypad4x1 = Keypad Membran 4x4
  Parça2 = Arduino Uno (Rev3)
  LCM1602_IIC1 = LCM1602 IIC [part_number="LCM1602 IIC" chip_label="LCM1602 IIC" package="DIP (Dual Inline) [THT]"]
  LCD1 = LCD screen

nets:
  N1: Parça1.D1/TX, Parça2.D0/RX
  N2: Parça1.D0/RX, Parça2.D1/TX
  N3: Parça1.D2, Keypad4x1.Pin8
  N4: Parça1.D3, Keypad4x1.Pin7
  N5: Parça1.D4, Keypad4x1.Pin6
  N6: Parça1.D5, Keypad4x1.Pin5
  N7: Parça1.D6, Keypad4x1.Pin4
  N8: Parça1.D7, Keypad4x1.Pin3
  N9: Parça1.D8, Keypad4x1.Pin2
  N10: Parça1.D9, Keypad4x1.Pin1
  GND: Parça1.GND, Parça2.GND, LCM1602_IIC1.GND
  N11: Parça2.A4/SDA, LCM1602_IIC1.SDA
  N12: Parça2.A5/SCL, LCM1602_IIC1.SCL
  5V: Parça2.5V, LCM1602_IIC1.VCC
  VSS: LCM1602_IIC1.VSS, LCD1.VSS
  VDD: LCM1602_IIC1.VDD, LCD1.VDD
  N13: LCM1602_IIC1.V0, LCD1.V0
  N14: LCM1602_IIC1.RS, LCD1.RS
  N15: LCM1602_IIC1.RW, LCD1.R/W
  N16: LCM1602_IIC1.E, LCD1.E
  N17: LCM1602_IIC1.D0, LCD1.DB0
  N18: LCM1602_IIC1.D1, LCD1.DB1
  N19: LCM1602_IIC1.D2, LCD1.DB2
  N20: LCM1602_IIC1.D3, LCD1.DB3
  N21: LCM1602_IIC1.D4, LCD1.DB4
  N22: LCM1602_IIC1.D5, LCD1.DB5
  N23: LCM1602_IIC1.D6, LCD1.DB6
  N24: LCM1602_IIC1.D7, LCD1.DB7
  N25: LCM1602_IIC1.A, LCD1.LED+
  N26: LCM1602_IIC1.K, LCD1.LED-
  N27: LCM1602_IIC1.LED_A, LCM1602_IIC1.LED_B

custom parts:
  Keypad Membran 4x4: Membrane Keypad 4x4 Matrix
  LCM1602 IIC: I2C-Module to use a 1602 or 2004 LCD on with the wire.h libory Serial LCD Modul
